# Fritzing sketch arduino_ds18b20_sensor (saved by Fritzing 0.9.0b)
breadboards: 1

parts:
  Arduino_Pro_Mini = Arduino Pro Mini v13
  R1 = Resistor [tolerance=±5% resistance=4.7k package=THT]
  DS2 = DS18B20 1-Wire Temperature Sensor [part_number=DS18B20]
  FTDI_USB/Serial = FTDI Basic Programmer

nets:
  N1: Arduino_Pro_Mini.DTR, FTDI_USB/Serial.DTR
  N2: Arduino_Pro_Mini.D0/TX, FTDI_USB/Serial.RXI
  N3: Arduino_Pro_Mini.D1/RX, FTDI_USB/Serial.TXO
  VCC: Arduino_Pro_Mini.VCC, R1.Pin_0, DS2.VDD, FTDI_USB/Serial.POWER
  GND: Arduino_Pro_Mini.GND, DS2.GND, FTDI_USB/Serial.GND
  N4: Arduino_Pro_Mini.D2, R1.Pin_1, DS2.DQ

custom parts:
  DS18B20 1-Wire Temperature Sensor: DS18B20 1-Wire Temperature Sensor - waterproof version
